// Logisim project projeto-gtn-xtreme.circ as structural Verilog: 9 circuits, main circuit main
module main (
);

  wire button_1_out, clock_1_out, dipswitch_2_p1;
  wire [3:0] dipswitch_1_p1, registrador4_1_q;

  // DipSwitch dipswitch_1: pin names not known; wires that end beside it: dipswitch_1_p1[0], dipswitch_1_p1[1], dipswitch_1_p1[2], dipswitch_1_p1[3]
  Clock clock_1 (.out(clock_1_out));
  // DipSwitch #(.NSwitches(1)) dipswitch_2: pin names not known; wires that end beside it: dipswitch_2_p1
  Registrador4 registrador4_1 (
    .D(dipswitch_1_p1), .Enable(dipswitch_2_p1), .Clock(clock_1_out), .Q(registrador4_1_q),
    .Reset(button_1_out));
  Button button_1 (.out(button_1_out));
  Hex_Digit_Display hex_digit_display_1 (.value(registrador4_1_q));  // open: dp
endmodule

module Registrador4 (
  input  [3:0] D,
  input  Enable,
  input  Clock,
  input  Reset,
  output [3:0] Q
);

  Register #(.width(4), .Select("low")) register_1 (.D(D), .en(Enable), .Q(Q), .clk(Clock), .clr(Reset));
endmodule

module Contador (
  input  Enable,
  input  Clock,
  input  Reset,
  output [3:0] out_4
);

  Counter #(.width(4), .max('h9)) counter_1 (
    .count(Enable), .Q(out_4), .clk(Clock), .clr(Reset), .down(1'b1));  // open: load, D, carry, preset
endmodule

module Somador4b5b (
  input  [3:0] A,
  input  [3:0] B,
  output [4:0] out_3
);

  Adder #(.width(4)) adder_1 (.a(A), .b(B), .out(out_3[3:0]), .cout(out_3[4]));  // open: cin
endmodule

module Comparador_5b (
  input  [4:0] A,
  input  [4:0] B,
  output Igual
);

  Comparator #(.width(5)) comparator_1 (.a(A), .b(B), .eq(Igual));  // open: gt, lt
endmodule

module Diferenca_5b (
  input  [4:0] A,
  input  [4:0] B,
  output [4:0] DIFF
);

  wire SEL;
  wire [4:0] DAB, DBA;

  Multiplexer #(.width(5), .enable("false")) multiplexer_1 (.in0(DAB), .in1(DBA), .out(DIFF), .sel(SEL));
  Subtractor #(.width(5)) subtractor_1 (.a(A), .b(B), .out(DAB), .bin(1'b0), .bout(SEL));
  Subtractor #(.width(5)) subtractor_2 (.a(B), .b(A), .out(DBA), .bin(1'b0));  // open: bout
endmodule

module cores_5b (
  input  [4:0] a,
  output [7:0] out_2,
  output [7:0] out_3
);

  wire [7:0] bit_extender_1_out, shifter_1_out;

  assign bit_extender_1_out = {{3{1'b0}}, a};  // Bit_Extender bit_extender_1
  Shifter shifter_1 (.in(bit_extender_1_out), .\dist (3'b011), .out(shifter_1_out));
  assign out_2 = shifter_1_out | 8'h7;  // OR_Gate or_1, 8 bits wide
  assign out_3 = ~out_2;  // NOT_Gate not_1, 8 bits wide
endmodule

module comparador_4b (
  input  [3:0] A,
  input  [3:0] B,
  output Igual
);

  Comparator #(.width(4)) comparator_1 (.a(A), .b(B), .eq(Igual));  // open: gt, lt
endmodule

module GTN_X (
  input  Confirmar,
  input  Novo,
  input  [3:0] X,
  input  [3:0] Y,
  output [7:0] out_5,
  output [7:0] out_6,
  output X_2,
  output Y_2,
  output S
);

  wire comparador_4b_1_igual, comparador_4b_2_igual, comparador_5b_1_igual;
  wire [4:0] diferenca_5b_1_diff, somador4b5b_1_out_3, somador4b5b_2_out_3;
  wire [7:0] bit_extender_1_out, cores_5b_1_out_2, cores_5b_1_out_3, random_1_out;

  Random random_1 (.clk(Novo), .out(random_1_out));  // open: next, clr
  assign bit_extender_1_out = {{7{Confirmar}}, Confirmar};  // Bit_Extender bit_extender_1
  and and_1 (X_2, Confirmar, comparador_4b_1_igual);
  comparador_4b comparador_4b_1 (.A(random_1_out[3:0]), .B(X), .Igual(comparador_4b_1_igual));
  Somador4b5b somador4b5b_1 (.A(random_1_out[7:4]), .B(random_1_out[3:0]), .out_3(somador4b5b_1_out_3));
  Somador4b5b somador4b5b_2 (.A(Y), .B(X), .out_3(somador4b5b_2_out_3));
  and and_2 (Y_2, Confirmar, comparador_4b_2_igual);
  and and_3 (S, Confirmar, comparador_5b_1_igual);
  comparador_4b comparador_4b_2 (.A(random_1_out[7:4]), .B(Y), .Igual(comparador_4b_2_igual));
  Comparador_5b comparador_5b_1 (.A(somador4b5b_1_out_3), .B(somador4b5b_2_out_3), .Igual(comparador_5b_1_igual));
  assign out_5 = bit_extender_1_out & cores_5b_1_out_2;  // AND_Gate and_4, 8 bits wide
  Diferenca_5b diferenca_5b_1 (.A(somador4b5b_1_out_3), .B(somador4b5b_2_out_3), .DIFF(diferenca_5b_1_diff));
  assign out_6 = cores_5b_1_out_3 & bit_extender_1_out;  // AND_Gate and_5, 8 bits wide
  cores_5b cores_5b_1 (.a(diferenca_5b_1_diff), .out_2(cores_5b_1_out_2), .out_3(cores_5b_1_out_3));
endmodule
